# Fritzing sketch sketch (saved by Fritzing 0.8.7b)
breadboards: 1

parts:
  DI2 = 7-Segment LED Display [package=THT]
  Part1 = Arduino Uno (Rev3)
  R1 = Resistor [tolerance=±5% resistance=220 package=THT]

nets:
  N1: DI2.cathodeE, Part1.D6_PWM
  N2: DI2.cathodeD, Part1.D5_PWM
  N3: DI2.commAnode#2, R1.Pin_1
  N4: DI2.cathodeC, Part1.D4
  N5: DI2.cathodeDP, Part1.D9_PWM
  N6: DI2.cathodeB, Part1.D3_PWM
  N7: DI2.cathodeA, Part1.D2
  N8: DI2.cathodeF, Part1.D7
  N9: DI2.cathodeG, Part1.D8
  N10: Part1.5V, R1.Pin_0
